# Fritzing sketch 4X4 Keypad (saved by Fritzing 0.9.3b)
breadboards: 1

parts:
  Keypad4x1 = Keypad Membran 4x4
  Raspberry_Pi_1 = Raspberry Pi 3 [part_number=RPI-3-V1.2]
  R1 = Resistor [tolerance=±5% resistance=1k package="0603 [SMD]"]
  R2 = Resistor [tolerance=±5% resistance=1k package="0603 [SMD]"]
  R3 = Resistor [tolerance=±5% resistance=1k package="0603 [SMD]"]
  R4 = Resistor [tolerance=±5% resistance=1k package="0603 [SMD]"]

nets:
  N1: Keypad4x1.Pin1, R1.Pin_1
  N2: Keypad4x1.Pin2, R4.Pin_1
  N3: Keypad4x1.Pin3, R2.Pin_1
  N4: Keypad4x1.Pin4, R3.Pin_1
  N5: Keypad4x1.Pin5, Raspberry_Pi_1.GPIO14
  N6: Keypad4x1.Pin6, Raspberry_Pi_1.GPIO15
  N7: Keypad4x1.Pin7, Raspberry_Pi_1.GPIO18
  N8: Keypad4x1.Pin8, Raspberry_Pi_1.GPIO23
  N9: Raspberry_Pi_1.GPIO6, R3.Pin_0
  N10: Raspberry_Pi_1.GPIO13, R2.Pin_0
  N11: Raspberry_Pi_1.GPIO19, R4.Pin_0
  N12: Raspberry_Pi_1.GPIO26, R1.Pin_0

custom parts:
  Keypad Membran 4x4: Membrane Keypad 4x4 Matrix
