# Fritzing sketch 7 Segment Display (saved by Fritzing 0.9.3b)
breadboards: 1

parts:
  Raspberry_Pi_1 = Raspberry Pi 3 [part_number=RPI-3-V1.2]
  DI1 = 7-Segment LED Display [package=THT]
  R1 = Resistor [tolerance=±5% resistance=1k package="2010 [SMD]"]
  R2 = Resistor [tolerance=±5% resistance=1k package="2010 [SMD]"]
  R3 = Resistor [tolerance=±5% resistance=1k package="2010 [SMD]"]
  R4 = Resistor [tolerance=±5% resistance=1k package="2010 [SMD]"]
  R5 = Resistor [tolerance=±5% resistance=1k package="2010 [SMD]"]
  R6 = Resistor [tolerance=±5% resistance=1k package="2010 [SMD]"]
  R7 = Resistor [tolerance=±5% resistance=1k package="2010 [SMD]"]
  R8 = Resistor [tolerance=±5% resistance=1k package="2010 [SMD]"]

nets:
  N1: Raspberry_Pi_1.3v3, DI1.commAnode#7
  N2: Raspberry_Pi_1.GPIO6, R3.Pin_1
  N3: Raspberry_Pi_1.GPIO13, R4.Pin_1
  N4: Raspberry_Pi_1.GPIO19, R2.Pin_0
  N5: Raspberry_Pi_1.GPIO26, R1.Pin_0
  N6: Raspberry_Pi_1.GPIO21, R7.Pin_0
  N7: Raspberry_Pi_1.GPIO20, R8.Pin_0
  N8: Raspberry_Pi_1.GPIO16, R6.Pin_1
  N9: Raspberry_Pi_1.GPIO12, R5.Pin_1
  N10: DI1.cathodeE, R7.Pin_1
  N11: DI1.cathodeD, R8.Pin_1
  N12: DI1.cathodeC, R6.Pin_0
  N13: DI1.cathodeDP, R5.Pin_0
  N14: DI1.cathodeB, R3.Pin_0
  N15: DI1.cathodeA, R4.Pin_0
  N16: DI1.cathodeF, R2.Pin_1
  N17: DI1.cathodeG, R1.Pin_1
