# Fritzing sketch BMP180 (saved by Fritzing 0.9.3b)

parts:
  Raspberry_Pi_1 = Raspberry Pi 3 [part_number=RPI-3-V1.2]
  Part1 = Barometric Pressure Sensor - BMP180 Breakout (GY-68)

nets:
  3V3: Raspberry_Pi_1.3v3, Raspberry_Pi_1.GPIO2, Raspberry_Pi_1.5V, Part1.VCC, Part1.SDA
  N1: Raspberry_Pi_1.GPIO3, Part1.SCL
  GND: Raspberry_Pi_1.GND, Part1.GND
