# Fritzing sketch Compass (saved by Fritzing 0.9.3b)

parts:
  Raspberry_Pi_1 = Raspberry Pi 3 [part_number=RPI-3-V1.2]
  GY-1 = GY-271 [part_number=GY-271]

nets:
  N1: Raspberry_Pi_1.GPIO2, GY-1.SDA
  N2: Raspberry_Pi_1.GPIO3, GY-1.SCL
  GND: Raspberry_Pi_1.GND, GY-1.GND
  5V: Raspberry_Pi_1.5V, GY-1.VCC

custom parts:
  GY-271: GY-271 - Electronic compass module - 3 Axis Magnetic Field Sensor HMC5883L
