# Fritzing sketch DC Motor (saved by Fritzing 0.9.3b)
breadboards: 1

parts:
  Raspberry_Pi_1 = Raspberry Pi 3 [part_number=RPI-3-V1.2]
  M2 = DC Motor
  M3 = DC Motor
  VCC1 = Battery block 9V
  IC1 = L293D [package=THT]

nets:
  N1: Raspberry_Pi_1.GIPO10, IC1.In_3
  N2: Raspberry_Pi_1.GIPO9, IC1.In_4
  N3: Raspberry_Pi_1.GIPO11, IC1.Enable_2
  N4: Raspberry_Pi_1.GIPO25, IC1.Enable_1
  N5: Raspberry_Pi_1.GIPO24, IC1.In_1
  N6: Raspberry_Pi_1.GIPO23, IC1.In_2
  N7: Raspberry_Pi_1.GND, VCC1.-, IC1.0V
  N8: Raspberry_Pi_1.5V, IC1.+V
  N9: M2.pin_1, IC1.Out_2_(_Controlled_by_Enable_1_)
  N10: M2.pin_2, IC1.Out_1_(_Controlled_by_Enable_1_)
  N11: M3.pin_1, IC1.Out_4_(_Controlled_by_Enable_2_)
  N12: M3.pin_2, IC1.Out_3_(_Controlled_by_Enable_2_)
  N13: VCC1.+, IC1.+Vmotor
