# Fritzing sketch Fingerprint Sensor (saved by Fritzing 0.9.3b)

parts:
  Raspberry_Pi_1 = Raspberry Pi 3 [part_number=RPI-3-V1.2]  # not connected
  Part1 = USB converter CP2102
  Part2 = sensor_biometrico

nets:
  +5V: Part1.+5V, Part2.VCC
  GND: Part1.GND, Part2.GND
  N1: Part1.TXO, Part2.RX
  N2: Part1.RXI, Part2.TX

notes:
  FINGERPRINT SENSOR

custom parts:
  sensor_biometrico: Adafruit Optical Fingerprint Sensor
