# Fritzing sketch Gas Sensor (Smoke) (saved by Fritzing 0.9.3b)
breadboards: 1

parts:
  Raspberry_Pi_1 = Raspberry Pi 3 [part_number=RPI-3-V1.2]
  IC1 = MCP3008 8-channel 10-bit ADC [part_number=MCP3008]
  Part2 = TXB0108 8-channel Bi-directional Logic Level Converter
  Part1 = MQ-3 breakout

nets:
  N1: Raspberry_Pi_1.3v3, IC1.no_name_yet#15, IC1.no_name_yet#16, Part2.VCCA
  N2: Raspberry_Pi_1.GIPO10, IC1.no_name_yet#11
  N3: Raspberry_Pi_1.GIPO9, IC1.no_name_yet#12
  N4: Raspberry_Pi_1.GIPO11, IC1.no_name_yet#13
  N5: Raspberry_Pi_1.GIPO8, IC1.no_name_yet#10
  GND: Raspberry_Pi_1.GND, IC1.no_name_yet#9, IC1.no_name_yet#14, Part2.GND, Part1.GND
  5V: Raspberry_Pi_1.5V, Part2.VCCB, Part1.VCC
  N6: IC1.no_name_yet#1, Part2.A1
  N7: Part2.B1, Part1.AO

custom parts:
  TXB0108 8-channel Bi-directional Logic Level Converter: Because the Arduino (and Basic Stamp) are 5V devices, and most modern sensors, displays, flash cards and modes are 3.3V-only, many makers find that they need to perform level shifting/conversion to protect the 3.3V device from 5V. Although one can use resistors to make a divider, for high speed transfers, the resistors can add a lot of slew and cause havoc that is tough to debug. For that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
  MQ-3 breakout: Alcohol sensor is capable of detecting alcohol (ethanol) particles on itself and gives the information in digital form back to us to manipulate with it. SKU:101251 • Voltage: 5V DC • Power: max 750mW • Measurement range: 0.04-4mg/L
