# Fritzing sketch Soil Moisture Sensor (saved by Fritzing 0.9.3b)

parts:
  부품2 = FC-28 Soil Hygrometer Module
  Raspberry_Pi_1 = Raspberry Pi 3 [part_number=RPI-3-V1.2]
  부품1 = FC-28 Soil Hygrometer Module - Probe

nets:
  VCC: 부품2.VCC, Raspberry_Pi_1.5V
  GND: 부품2.GND, Raspberry_Pi_1.GND
  N1: 부품2.DO, Raspberry_Pi_1.GIPO21
  N2: 부품2.POS, 부품1.POS
  N3: 부품2.NEG, 부품1.NEG

custom parts:
  FC-28 Soil Hygrometer Module: The FC-28 is a soil hygrometer module that uses the Texas Instruments LM393 comparator chip to provide an analog measurement of soil humidity. The digital output is high when soil moisture is over a certain threshold, as determined by adjusting the potentiometer.
  FC-28 Soil Hygrometer Module - Probe: The FC-28 is a soil hygrometer module that uses the Texas Instruments LM393 comparator chip to provide an analog measurement of soil humidity.
