# Fritzing sketch Vibration Sensor (saved by Fritzing 0.9.3b)

parts:
  SW-1 = Vibration sensor module
  Raspberry_Pi_1 = Raspberry Pi 3 [part_number=RPI-3-V1.2]

nets:
  VCC: SW-1.vcc, Raspberry_Pi_1.5V
  N1: SW-1.Ground, Raspberry_Pi_1.GND
  N2: SW-1.Digital_output, Raspberry_Pi_1.GPIO17

custom parts:
  Vibration sensor module: Single-roller type full induction trigger switch. When no vibration or tilt, the product is ON conduction state, and in the steady state, when a vibration or tilt, the switch will be rendered instantly disconnect the conductive resistance increases, generating a current pulse signal, thereby triggering circuit. The default state of the swith is close Digital output Supply voltage:3.3V-5V On-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
