# Fritzing sketch Water Flow Meter (saved by Fritzing 0.9.3b)
breadboards: 1

parts:
  Raspberry_Pi_1 = Raspberry Pi 3 [part_number=RPI-3-V1.2]
  YF-S201_Flow_Meter1 = YF-S201 Water Flow Meter
  R1 = Resistor [tolerance=±5% resistance=10k package="2512 [SMD]"]
  R2 = Resistor [tolerance=±5% resistance=4.7k package="2512 [SMD]"]

nets:
  N1: Raspberry_Pi_1.GPIO17, R1.Pin_1, R2.Pin_0
  GND: Raspberry_Pi_1.GND, YF-S201_Flow_Meter1.GND, R1.Pin_0
  5V: Raspberry_Pi_1.5V, YF-S201_Flow_Meter1.VCC
  N2: YF-S201_Flow_Meter1.SIG, R2.Pin_1

custom parts:
  YF-S201 Water Flow Meter: The YF-S201 Flow Meter. The input voltage is 5V to 24V (DC).
