# Fritzing sketch Alarm (saved by Fritzing 0.9.3b)
breadboards: 1

parts:
  Raspberry_Pi_1 = Raspberry Pi 3 [part_number=RPI-3-V1.2]
  DHT1 = DHT11 Humitidy and Temperature Sensor
  LED1 = smd LED [color="Red (633nm)" package="0603 [SMD]"]
  J1 = Piezo Speaker

nets:
  N1: Raspberry_Pi_1.GIPO4, DHT1.DATA
  N2: Raspberry_Pi_1.GIPO17, LED1.anode
  N3: Raspberry_Pi_1.GIPO27, J1.pin2
  GND: Raspberry_Pi_1.GND, DHT1.GND, LED1.cathode, J1.pin1
  5V: Raspberry_Pi_1.5V, DHT1.VDD

custom parts:
  DHT11 Humitidy and Temperature Sensor: DHT11 Humidity and Temperature Sensor
