# Fritzing sketch alert (saved by Fritzing 0.9.3b)
breadboards: 1

parts:
  Raspberry_Pi_1 = Raspberry Pi 3 [part_number=RPI-3-V1.2]
  Part1 = SRF05 Ultrasonic Rangefinder
  J1 = Piezo Speaker
  R1 = Resistor [tolerance=±5% resistance=220 package="0603 [SMD]"]
  LCM1602_IIC1 = LCM1602 IIC [part_number="LCM1602 IIC" chip_label="LCM1602 IIC" package="DIP (Dual Inline) [THT]"]
  LCD1 = LCD screen

nets:
  N1: Raspberry_Pi_1.GPIO2, LCM1602_IIC1.SDA
  N2: Raspberry_Pi_1.GPIO3, LCM1602_IIC1.SCL
  N3: Raspberry_Pi_1.GIPO17, Part1.Trig
  N4: Raspberry_Pi_1.GIPO27, R1.Pin_1
  N5: Raspberry_Pi_1.GIPO18, J1.pin2
  GND: Raspberry_Pi_1.GND, Part1.GND, J1.pin1, LCM1602_IIC1.GND
  VCC: Raspberry_Pi_1.5V, Part1.VCC, LCM1602_IIC1.VCC
  N6: Part1.Echo, R1.Pin_0
  VSS: LCM1602_IIC1.VSS, LCD1.VSS
  VDD: LCM1602_IIC1.VDD, LCD1.VDD
  N7: LCM1602_IIC1.V0, LCD1.V0
  N8: LCM1602_IIC1.RS, LCD1.RS
  N9: LCM1602_IIC1.RW, LCD1.R/W
  N10: LCM1602_IIC1.E, LCD1.E
  N11: LCM1602_IIC1.D0, LCD1.DB0
  N12: LCM1602_IIC1.D1, LCD1.DB1
  N13: LCM1602_IIC1.D2, LCD1.DB2
  N14: LCM1602_IIC1.D3, LCD1.DB3
  N15: LCM1602_IIC1.D4, LCD1.DB4
  N16: LCM1602_IIC1.D5, LCD1.DB5
  N17: LCM1602_IIC1.D6, LCD1.DB6
  N18: LCM1602_IIC1.D7, LCD1.DB7
  N19: LCM1602_IIC1.A, LCD1.LED+
  N20: LCM1602_IIC1.K, LCD1.LED-

custom parts:
  LCM1602 IIC: I2C-Module to use a 1602 or 2004 LCD on with the wire.h libory Serial LCD Modul
