# Fritzing sketch Communication (saved by Fritzing 0.9.3b)
breadboards: 1

parts:
  R1 = Resistor [tolerance=±5% resistance=220 package="0805 [SMD]"]
  R2 = Resistor [tolerance=±5% resistance=1k package="0805 [SMD]"]
  Part1 = Arduino Uno (Rev3)
  R3 = Photocell (LDR) [package=THT]
  LED1 = LED - 3mm [color="Red (633nm)" package="3 mm [THT]"]
  Raspberry_Pi_1 = Raspberry Pi 3 [part_number=RPI-3-V1.2]  # not connected

nets:
  N1: R1.Pin_0, LED1.anode
  N2: R2.Pin_0, Part1.A0, R3.pin_1
  N3: R2.Pin_1, Part1.GND
  N4: Part1.5V, R3.pin_0
