# Fritzing sketch Button (saved by Fritzing 0.9.3b)
breadboards: 1

parts:
  S1 = Pushbutton [package="[THT]"]
  R3 = Resistor [tolerance=±10% resistance=4.7k package="0603 [SMD]"]
  Raspberry_Pi_1 = Raspberry Pi 3 [part_number=RPI-3-V1.2]

nets:
  N1: S1.Pin_1, S1.Pin_2, Raspberry_Pi_1.GND
  N2: S1.Pin_3, S1.Pin_4, R3.Pin_1, Raspberry_Pi_1.GPIO10
  N3: R3.Pin_0, Raspberry_Pi_1.3v3
