# Fritzing sketch Buzzer (saved by Fritzing 0.9.3b)
breadboards: 1

parts:
  Raspberry_Pi_2 = Raspberry Pi 3 [part_number=RPI-3-V1.2]
  J1 = Piezo Speaker

nets:
  N1: Raspberry_Pi_2.GIPO22, J1.pin2
  N2: Raspberry_Pi_2.GND, J1.pin1
