# Fritzing sketch LCD (saved by Fritzing 0.9.3b)

parts:
  U2 = LCD-16X2 [package=lcd-16x2_noholes]
  LCM1602_IIC1 = LCM1602 IIC [part_number="LCM1602 IIC" chip_label="LCM1602 IIC" package="DIP (Dual Inline) [THT]"]
  Raspberry_Pi_1 = Raspberry Pi 3 [part_number=RPI-3-V1.2]

nets:
  VSS: U2.VSS, LCM1602_IIC1.VSS
  VDD: U2.VDD, LCM1602_IIC1.VDD
  N1: U2.VO, LCM1602_IIC1.V0
  N2: U2.RS, LCM1602_IIC1.RS
  N3: U2.R_W, LCM1602_IIC1.RW
  N4: U2.E, LCM1602_IIC1.E
  N5: U2.DB0, LCM1602_IIC1.D0
  N6: U2.DB1, LCM1602_IIC1.D1
  N7: U2.DB2, LCM1602_IIC1.D2
  N8: U2.DB3, LCM1602_IIC1.D3
  N9: U2.DB4, LCM1602_IIC1.D4
  N10: U2.DB5, LCM1602_IIC1.D5
  N11: U2.DB6, LCM1602_IIC1.D6
  N12: U2.DB7, LCM1602_IIC1.D7
  N13: U2.A, LCM1602_IIC1.A
  N14: U2.K, LCM1602_IIC1.K
  GND: LCM1602_IIC1.GND, Raspberry_Pi_1.GND
  VCC: LCM1602_IIC1.VCC, Raspberry_Pi_1.5V
  N15: LCM1602_IIC1.SDA, Raspberry_Pi_1.GPIO2
  N16: LCM1602_IIC1.SCL, Raspberry_Pi_1.GPIO3

custom parts:
  LCM1602 IIC: I2C-Module to use a 1602 or 2004 LCD on with the wire.h libory Serial LCD Modul
