# Fritzing sketch LDR (saved by Fritzing 0.9.3b)
breadboards: 1

parts:
  Raspberry_Pi_2 = Raspberry Pi 3 [part_number=RPI-3-V1.2]
  R1 = Photocell (LDR) [package=THT]
  C1 = Electrolytic Capacitor [capacitance=470µF voltage=20V package="200 mil [THT, electrolytic]"]

nets:
  N1: Raspberry_Pi_2.3v3, R1.pin_1
  N2: Raspberry_Pi_2.GPIO3, R1.pin_0, C1.+
  N3: Raspberry_Pi_2.GND, C1.-
