# Fritzing sketch LED with C (saved by Fritzing 0.9.3b)
breadboards: 1

parts:
  R1 = Resistor [tolerance=±5% resistance=330 package=THT]
  LED1 = smd LED [color="Blue (470nm)" package="1206 [SMD]"]
  Raspberry_Pi_3 = Raspberry Pi 3 [part_number=RPI-3-V1.2]

nets:
  N1: R1.Pin_0, LED1.cathode
  N2: R1.Pin_1, Raspberry_Pi_3.GND
  N3: LED1.anode, Raspberry_Pi_3.GPIO4
