# Fritzing sketch Plotly (saved by Fritzing 0.9.3b)

parts:
  Raspberry_Pi_1 = Raspberry Pi 3 [part_number=RPI-3-V1.2]
  DHT1 = DHT11 Humitidy and Temperature Sensor

nets:
  3V3: Raspberry_Pi_1.3v3, DHT1.VDD
  N1: Raspberry_Pi_1.GPIO4, Raspberry_Pi_1.GPIO14, DHT1.DATA
  GND: Raspberry_Pi_1.GND, DHT1.GND

custom parts:
  DHT11 Humitidy and Temperature Sensor: DHT11 Humidity and Temperature Sensor
