# Fritzing sketch RPi with Arduino (saved by Fritzing 0.9.3b)

parts:
  Raspberry_Pi_1 = Raspberry Pi 3 [part_number=RPI-3-V1.2]
  Part1 = Arduino Uno (Rev3)

nets:
  3V3: Raspberry_Pi_1.3v3, Part1.5V
  N1: Raspberry_Pi_1.GPIO2, Part1.A4/SDA
  N2: Raspberry_Pi_1.GPIO3, Part1.A5/SCL
  GND: Raspberry_Pi_1.GND, Part1.GND
