# Fritzing sketch Relay (saved by Fritzing 0.9.3b)

parts:
  Raspberry_Pi_1 = Raspberry Pi 3 [part_number=RPI-3-V1.2]
  KY-1 = Keyes Relay [package=THT]
  LED1 = LEDs [package=led10mm]

nets:
  N1: Raspberry_Pi_1.GIPO24, KY-1.signal
  N2: Raspberry_Pi_1.GND, KY-1.ground
  N3: Raspberry_Pi_1.5V, KY-1.power
  N4: KY-1.C, LED1.A

notes:
  Power Supply
  (240V)

custom parts:
  Keyes Relay: The Keyes 5V relay module is suitable for SCM development, home appliance control. It uses a 5V~12V TIL control signal which can control DC / AC signal.
  LEDs: LEDs Standard schematic elements and footprints for 5mm, 3mm, 1206, and 0603 sized LEDs. 5mm - Spark Fun Electronics SKU : COM-00529 (and others)
