# Fritzing sketch Ultrasonic Sensor (saved by Fritzing 0.9.3b)
breadboards: 1

parts:
  Raspberry_Pi_1 = Raspberry Pi 3 [part_number=RPI-3-V1.2]
  R1 = Resistor [tolerance=±5% resistance=1k package="1206 [SMD]"]
  Part1 = SRF05 Ultrasonic Rangefinder

nets:
  N1: Raspberry_Pi_1.GIPO17, Part1.Trig
  N2: Raspberry_Pi_1.GIPO27, R1.Pin_1
  GND: Raspberry_Pi_1.GND, Part1.GND
  5V: Raspberry_Pi_1.5V, Part1.VCC
  N3: R1.Pin_0, Part1.Echo
